// Digital circuit ALU.dig as structural Verilog
module ALU (
  input  [7:0] N,
  input  [7:0] AC,
  input  Shift,
  input  [7:0] MQSel,
  input  B3,
  input  B2,
  input  B1,
  output Of,
  output Of2,
  output [7:0] AC_out,
  output [7:0] MQ
);

  wire [7:0] divisor8bits_1_a_out, divisor8bits_1_mq, mult8bits_1_ac, mult8bits_1_mq, nand8bits_1_s,
       shift_1_s, somador8bits_1_s, subtrator8bits_1_s, xor8bits_1_s;

  somador8bits somador8bits_1 (.A(AC), .B(N), .Cin(1'b0), .S(somador8bits_1_s), .Cout(Of));
  subtrator8bits subtrator8bits_1 (.A(AC), .B(N), .S(subtrator8bits_1_s), .Cout(Of2));
  NAND8bits nand8bits_1 (.A(AC), .B(N), .S(nand8bits_1_s));
  XOR8bits xor8bits_1 (.A(AC), .B(N), .S(xor8bits_1_s));
  divisor8bits divisor8bits_1 (.A(AC), .B(N), .MQ(divisor8bits_1_mq), .A_out(divisor8bits_1_a_out));
  shift shift_1 (.Esquerda_Direita(Shift), .E(AC), .S(shift_1_s));
  mult8bits mult8bits_1 (.A(AC), .B(N), .AC(mult8bits_1_ac), .MQ(mult8bits_1_mq));
  Multiplexer #(.Selector_Bits(3), .Bits(8)) multiplexer_1 (
    .sel({B3, B2, B1}), .in_0(somador8bits_1_s), .in_1(subtrator8bits_1_s), .in_2(nand8bits_1_s),
    .in_3(xor8bits_1_s), .in_4(divisor8bits_1_a_out), .in_5(shift_1_s), .in_6(mult8bits_1_ac),
    .in_7({8{1'b1}}), .out(AC_out));
  Seven_Seg_Hex seven_seg_hex_1 (.d(AC_out[7:4]), .dp(1'b0));
  Multiplexer #(.Selector_Bits(3), .Bits(8)) multiplexer_2 (
    .sel({B3, B2, B1}), .in_0({8{1'b0}}), .in_1({8{1'b0}}), .in_2({8{1'b0}}), .in_3({8{1'b0}}),
    .in_4(divisor8bits_1_mq), .in_5({8{1'b0}}), .in_6(mult8bits_1_mq), .in_7(MQSel), .out(MQ));
  Seven_Seg_Hex seven_seg_hex_2 (.d(AC_out[3:0]), .dp(1'b0));
  Seven_Seg_Hex seven_seg_hex_3 (.d(MQ[7:4]), .dp(1'b0));
  Seven_Seg_Hex seven_seg_hex_4 (.d(MQ[3:0]), .dp(1'b0));

  // Notes on the sheet:
  //   AC
  //   MQ
endmodule
