// Digital circuit ALU.dig as structural Verilog
module ALU (
  input  [7:0] N,
  input  [2:0] OP,
  input  CLK,
  input  LOAD,
  output [7:0] AC,
  output [7:0] MQ,
  output [15:0] M_out,
  output Of_sub,
  output Of_soma
);

  wire [7:0] Als, Ars, LSB, MSB, multiplexer_1_out, multiplexer_2_out, NAND, Q, R, soma, subtracao, XOR;

  assign NAND = ~(AC & N);  // NAnd nand_1, 8 bits wide
  assign XOR = AC ^ N;  // XOr xor_1, 8 bits wide
  Register #(.Bits(8)) register_1 (.D(multiplexer_1_out), .C(CLK), .en(LOAD), .Q(M_out[15:8]));
  somador8bits somador8bits_1 (.A(AC), .B(N), .Cin(1'b0), .S(soma), .Cout(Of_soma));
  subtrator8bits subtrator8bits_1 (.A(AC), .B(N), .S(subtracao), .Cout(Of_sub));
  Multiplexer #(.Selector_Bits(3), .Bits(8)) multiplexer_1 (
    .sel(OP), .in_0(M_out[15:8]), .in_1(M_out[15:8]), .in_2(MSB), .in_3(Q), .in_4(M_out[15:8]),
    .in_5(M_out[15:8]), .in_6(M_out[15:8]), .in_7(M_out[15:8]), .out(multiplexer_1_out));
  mult8bits mult8bits_1 (.A(AC), .B(N), .AC(LSB), .MQ(MSB));
  divisor8bits divisor8bits_1 (.A(AC), .B(N), .MQ(Q), .A_out(R));
  Register #(.Bits(8)) register_2 (.D(multiplexer_2_out), .C(CLK), .en(LOAD), .Q(AC));
  Multiplexer #(.Selector_Bits(3), .Bits(8)) multiplexer_2 (
    .sel(OP), .in_0(soma), .in_1(subtracao), .in_2(LSB), .in_3(R), .in_4(Ars), .in_5(Als), .in_6(NAND),
    .in_7(XOR), .out(multiplexer_2_out));
  leftshift leftshift_1 (.A(AC), .Als(Als));
  rightshift rightshift_1 (.A(AC), .Ars(Ars));

  assign M_out[7:0] = AC;
  assign MQ = M_out[15:8];

  // Other names for the same wires on the sheet: Of = Of_soma; Of2 = Of_sub
endmodule
