// Digital circuit CPU.dig as structural Verilog
module CPU (
  input  in_4,
  output [7:0] AC,
  output [7:0] MQ,
  output [3:0] out_3,
  output [7:0] out_5,
  output [7:0] out_6,
  output [7:0] out_7,
  output [4:0] out_8,
  output [7:0] out_9,
  output [2:0] out_10,
  output [2:0] out_11,
  output [3:0] out_12
);

  wire AC_LOAD, B, CLK, CLK_PC, IR_LOAD, MAR;
  wire [3:0] driver_3_out, MAR_q;
  wire [7:0] driver_2_out, driver_7_out;

  contador4bits contador4bits_1 (.Set(1'b0), .CLK(CLK_PC), .Clr(in_4), .O(out_3));
  Register #(.Bits(8)) IR (.D(out_6), .C(CLK), .en(IR_LOAD), .Q({out_11, out_8}));
  assign out_6 = IR_LOAD ? driver_2_out : 8'bz;  // Driver driver_1
  assign driver_2_out = MAR ? {4'b0000, out_3} : 8'bz;  // Driver driver_2
  assign {out_12, driver_3_out} = MAR ? driver_2_out : 8'bz;  // Driver driver_3
  Register #(.Bits(4)) u_MAR (.D(driver_3_out), .C(CLK), .en(MAR), .Q(MAR_q));
  EEPROMDualPort #(.AddrBits(4), .Bits(8)) \operações  (
    .A(MAR_q), .Din({8{1'b0}}), .str(1'b0), .C(CLK), .ld(IR_LOAD), .D(out_5));
  EEPROMDualPort #(.AddrBits(5), .Bits(8)) operandos (
    .A(out_8), .Din({8{1'b0}}), .str(1'b0), .C(CLK), .ld(B), .D(out_7));
  assign driver_2_out = B ? out_7 : 8'bz;  // Driver driver_4
  assign driver_2_out = IR_LOAD ? out_5 : 8'bz;  // Driver driver_5
  assign out_10 = AC_LOAD ? out_11 : 3'bz;  // Driver driver_6
  assign driver_7_out = B ? driver_2_out : 8'bz;  // Driver driver_7
  and and_1 (CLK_PC, IR_LOAD, CLK);
  Button button_1 (.out(CLK));
  Register #(.Bits(8)) REG_B (.D(driver_7_out), .C(CLK), .en(B), .Q(out_9));
  ring_counter ring_counter_1 (.CLK(CLK), .Set(in_4), .O0(MAR), .O1(IR_LOAD), .O2(B), .O3(AC_LOAD));
  ALU alu_1 (.N(out_9), .OP(out_10), .CLK(CLK), .LOAD(AC_LOAD), .AC(AC), .MQ(MQ));  // open: M_out, Of_sub, Of_soma
  Seven_Seg_Hex seven_seg_hex_1 (.d(AC[7:4]), .dp(1'b0));
  Seven_Seg_Hex seven_seg_hex_2 (.d(AC[3:0]), .dp(1'b0));
  Seven_Seg_Hex seven_seg_hex_3 (.d(MQ[7:4]), .dp(1'b0));
  Seven_Seg_Hex seven_seg_hex_4 (.d(MQ[3:0]), .dp(1'b0));

  // Other names for the same wires on the sheet: ALU = AC_LOAD; CLR = in_4; operando_EN = B; operações_EN = IR_LOAD;
  //   PC_INT = IR_LOAD; PC_EN = MAR

  // Notes on the sheet:
  //   contents of operações (hex, n*v repeats v):
  //   0,41,a0,22,80,63
  //   contents of operandos (hex, n*v repeats v):
  //   6,4,a,7
  //   1. Adição:  0 + 6 = 6
  //   2. Multiplicação: 6 x 4 = 24
  //   3. Shift Left: 24 x 2 = 48
  //   4. Subtração: 48 - 10 = 38
  //   5. Shift Right: 38/2 = 19
  //   6. Divisão: 19/7 = 2 e resto 5
endmodule
