// Digital circuit contador3bits.dig as structural Verilog
module contador3bits (
  input  C,
  output Q0,
  output Q1,
  output Q2,
  output CLK
);

  wire and_1_out, and_2_out, and_3_out, and_4_out, jk_ff_as_1_nq, jk_ff_as_2_nq, start_out;
  wire [3:0] driver_1_out, register_1_q, register_2_q, register_3_q, register_4_q;

  and and_1 (and_1_out, ~Q0, Q1, ~Q2);  // And
  and and_2 (and_2_out, ~Q0, ~Q1, ~Q2);  // And
  and and_3 (and_3_out, ~Q0, ~Q1, Q2);  // And
  and and_4 (and_4_out, Q0, ~Q1, ~Q2);  // And
  Button start (.out(start_out));
  Register #(.Bits(4)) register_1 (.D(4'b0000), .C(and_2_out), .en(1'b1), .Q(register_1_q));
  Register #(.Bits(4)) register_2 (.D(4'b0011), .C(and_3_out), .en(1'b1), .Q(register_2_q));
  Register #(.Bits(4)) register_3 (.D(4'b0001), .C(and_4_out), .en(1'b1), .Q(register_3_q));
  Register #(.Bits(4)) register_4 (.D(4'b0010), .C(and_1_out), .en(1'b1), .Q(register_4_q));
  JK_FF_AS jk_ff_as_1 (.Set(start_out), .J(1'b1), .C(C), .K(1'b1), .Clr(1'b0), .Q(Q0), .nQ(jk_ff_as_1_nq));
  assign driver_1_out = and_2_out ? register_1_q : 4'bz;  // Driver driver_1
  assign driver_1_out = and_3_out ? register_2_q : 4'bz;  // Driver driver_2
  assign driver_1_out = and_4_out ? register_3_q : 4'bz;  // Driver driver_3
  assign driver_1_out = and_1_out ? register_4_q : 4'bz;  // Driver driver_4
  LED led_1 (.in(Q0));
  JK_FF_AS jk_ff_as_2 (.Set(1'b0), .J(1'b1), .C(jk_ff_as_1_nq), .K(1'b1), .Clr(1'b0), .Q(Q1), .nQ(jk_ff_as_2_nq));
  LED led_2 (.in(Q1));
  JK_FF_AS jk_ff_as_3 (.Set(1'b0), .J(1'b1), .C(jk_ff_as_2_nq), .K(1'b1), .Clr(1'b0), .Q(Q2));  // open: nQ
  LED led_3 (.in(Q2));
  Seven_Seg_Hex seven_seg_hex_1 (.d(driver_1_out), .dp(1'b0));

  assign CLK = C;
endmodule
