// Digital circuit divisaointerna.dig as structural Verilog
module divisaointerna (
  input  [7:0] Ri,
  input  [7:0] N,
  output [7:0] Rt,
  output Q
);

  wire [7:0] subtrator8bits_1_s;

  subtrator8bits subtrator8bits_1 (.A(Ri), .B(N), .S(subtrator8bits_1_s), .Cout(Q));
  Multiplexer #(.Bits(8)) multiplexer_1 (.sel(Q), .in_0(Ri), .in_1(subtrator8bits_1_s), .out(Rt));
endmodule
