// Digital circuit divisor8bits.dig as structural Verilog
module divisor8bits (
  input  [7:0] A,
  input  [7:0] B,
  output [7:0] MQ,
  output [7:0] A_out
);

  wire [7:0] divisaointerna_1_rt, divisaointerna_2_rt, divisaointerna_3_rt, divisaointerna_4_rt,
       divisaointerna_5_rt, divisaointerna_6_rt, divisaointerna_7_rt;

  divisaointerna divisaointerna_1 (.Ri(A), .N({B[0], {7{1'b0}}}), .Rt(divisaointerna_1_rt), .Q(MQ[7]));
  divisaointerna divisaointerna_2 (
    .Ri(divisaointerna_1_rt), .N({B[1:0], {6{1'b0}}}), .Rt(divisaointerna_2_rt), .Q(MQ[6]));
  divisaointerna divisaointerna_3 (
    .Ri(divisaointerna_2_rt), .N({B[2:0], {5{1'b0}}}), .Rt(divisaointerna_3_rt), .Q(MQ[5]));
  divisaointerna divisaointerna_4 (
    .Ri(divisaointerna_3_rt), .N({B[3:0], 4'b0000}), .Rt(divisaointerna_4_rt), .Q(MQ[4]));
  divisaointerna divisaointerna_5 (.Ri(divisaointerna_4_rt), .N({B[4:0], 3'b000}), .Rt(divisaointerna_5_rt), .Q(MQ[3]));
  divisaointerna divisaointerna_6 (.Ri(divisaointerna_5_rt), .N({B[5:0], 2'b00}), .Rt(divisaointerna_6_rt), .Q(MQ[2]));
  divisaointerna divisaointerna_7 (.Ri(divisaointerna_6_rt), .N({B[6:0], 1'b0}), .Rt(divisaointerna_7_rt), .Q(MQ[1]));
  divisaointerna divisaointerna_8 (.Ri(divisaointerna_7_rt), .N(B), .Rt(A_out), .Q(MQ[0]));

  // Other names for the same wires on the sheet: B_shift_0[7:0] = B; B_shift_1[7:1] = B[6:0]; B_shift_2[7:2] = B[5:0];
  //   B_shift_3[7:3] = B[4:0]; B_shift_4[7:4] = B[3:0]; B_shift_5[7:5] = B[2:0]; B_shift_6[7:6] = B[1:0];
  //   B_shift_7[7] = B[0]; Q0 = MQ[0]; Q1 = MQ[1]; Q2 = MQ[2]; Q3 = MQ[3]; Q4 = MQ[4]; Q5 = MQ[5]; Q6 = MQ[6];
  //   Q7 = MQ[7]
endmodule
