// Digital circuit inversor.dig as structural Verilog
module inversor (
  input  [7:0] A,
  output [7:0] A_invertido
);

  wire [7:0] not_1_out;

  not not_1 (not_1_out[0], A[0]);
  not not_2 (not_1_out[1], A[1]);
  not not_3 (not_1_out[2], A[2]);
  not not_4 (not_1_out[3], A[3]);
  not not_5 (not_1_out[4], A[4]);
  not not_6 (not_1_out[5], A[5]);
  not not_7 (not_1_out[6], A[6]);
  not not_8 (not_1_out[7], A[7]);
  somador8bits somador8bits_1 (.A(not_1_out), .B({8{1'b0}}), .Cin(1'b1), .S(A_invertido));  // open: Cout
endmodule
