// Digital circuit registrador8bits.dig as structural Verilog
module registrador8bits (
  input  [7:0] D,
  input  CLK,
  input  En,
  output [7:0] Q
);

  wire d_ff_1_nq, d_ff_2_nq, d_ff_3_nq, d_ff_4_nq, d_ff_5_nq, d_ff_6_nq, d_ff_7_nq, d_ff_8_nq,
       multiplexer_1_out, multiplexer_2_out, multiplexer_3_out, multiplexer_4_out, multiplexer_5_out,
       multiplexer_7_out, multiplexer_8_out;

  Multiplexer multiplexer_1 (.sel(En), .in_0(d_ff_1_nq), .in_1(D[0]), .out(multiplexer_1_out));
  Multiplexer multiplexer_2 (.sel(En), .in_0(d_ff_2_nq), .in_1(D[1]), .out(multiplexer_2_out));
  Multiplexer multiplexer_3 (.sel(En), .in_0(d_ff_3_nq), .in_1(D[2]), .out(multiplexer_3_out));
  Multiplexer multiplexer_4 (.sel(En), .in_0(d_ff_4_nq), .in_1(D[3]), .out(multiplexer_4_out));
  Multiplexer multiplexer_5 (.sel(En), .in_0(d_ff_5_nq), .in_1(D[4]), .out(multiplexer_5_out));
  D_FF d_ff_1 (.D(multiplexer_1_out), .C(CLK), .Q(Q[0]), .nQ(d_ff_1_nq));
  D_FF d_ff_2 (.D(multiplexer_2_out), .C(CLK), .Q(Q[1]), .nQ(d_ff_2_nq));
  D_FF d_ff_3 (.D(multiplexer_3_out), .C(CLK), .Q(Q[2]), .nQ(d_ff_3_nq));
  D_FF d_ff_4 (.D(multiplexer_4_out), .C(CLK), .Q(Q[3]), .nQ(d_ff_4_nq));
  D_FF d_ff_5 (.D(multiplexer_5_out), .C(CLK), .Q(Q[4]), .nQ(d_ff_5_nq));
  Multiplexer multiplexer_6 (.sel(En), .in_0(d_ff_6_nq), .in_1(D[5]));  // open: out
  Multiplexer multiplexer_7 (.sel(En), .in_0(d_ff_7_nq), .in_1(D[6]), .out(multiplexer_7_out));
  Multiplexer multiplexer_8 (.sel(En), .in_0(d_ff_8_nq), .in_1(D[7]), .out(multiplexer_8_out));
  D_FF d_ff_6 (.D(D[5]), .C(CLK), .Q(Q[5]), .nQ(d_ff_6_nq));
  D_FF d_ff_7 (.D(multiplexer_7_out), .C(CLK), .Q(Q[6]), .nQ(d_ff_7_nq));
  D_FF d_ff_8 (.D(multiplexer_8_out), .C(CLK), .Q(Q[7]), .nQ(d_ff_8_nq));

  // Other names for the same wires on the sheet: D_0 = D[0]; D_1 = D[1]; D_2 = D[2]; D_3 = D[3]; D_4 = D[4];
  //   D_5 = D[5]; D_6 = D[6]; D_7 = D[7]; Q_0 = Q[0]; Q_1 = Q[1]; Q_2 = Q[2]; Q_3 = Q[3]; Q_4 = Q[4]; Q_5 = Q[5];
  //   Q_6 = Q[6]; Q_7 = Q[7]
endmodule
