// Digital circuit subtrator8bits.dig as structural Verilog
module subtrator8bits (
  input  [7:0] A,
  input  [7:0] B,
  output [7:0] S,
  output Cout
);

  wire [7:0] inversor_1_a_invertido, inversor_2_a_invertido, somador8bits_1_s;

  inversor inversor_1 (.A(B), .A_invertido(inversor_1_a_invertido));
  somador8bits somador8bits_1 (.A(A), .B(inversor_1_a_invertido), .Cin(1'b0), .S(somador8bits_1_s), .Cout(Cout));
  inversor inversor_2 (.A(somador8bits_1_s), .A_invertido(inversor_2_a_invertido));
  Multiplexer #(.Bits(8)) multiplexer_1 (
    .sel(somador8bits_1_s[7]), .in_0(somador8bits_1_s), .in_1(inversor_2_a_invertido), .out(S));
  LED plus (.in(somador8bits_1_s[7]));
endmodule
