// Digital circuit mult8bits.dig as structural Verilog
module mult8bits (
  input  [7:0] A,
  input  [7:0] B,
  output [7:0] AC,
  output [7:0] MQ
);

  wire H1, h1_t, H2, h2_t, H3, h3_t, H4, h4_t, H5, h5_t, H6, h6_t, H7, h7_t, H8, h8_t, L1, l1_t, L2, l2_t,
       L3, l3_t, L4, l4_t, L5, l5_t, L6, l6_t, L7, l7_t, L8, l8_t, P1, p1_t, P2, p2_t, P3, p3_t, P4, p4_t,
       P5, p5_t, P6, p6_t, P7, p7_t, P8, p8_t, W0;
  wire [7:0] PP1, PP2, PP3, PP4, PP5, PP6, PP7;
  wire [7:1] PP0;
  wire [8:8] somador9bits_1_o, somador9bits_2_o, somador9bits_3_o, somador9bits_4_o, somador9bits_5_o,
       somador9bits_6_o;

  somador9bits somador9bits_1 (
    .A({2'b00, PP0}), .B({1'b0, PP1}), .O(somador9bits_1_o[8]),
    .S({p8_t, p7_t, p6_t, p5_t, p4_t, p3_t, p2_t, p1_t, AC[1]}));
  and and_1 (AC[0], A[0], B[0]);
  and and_2 (PP0[1], A[0], B[1]);
  and and_3 (PP0[2], A[0], B[2]);
  and and_4 (PP0[3], A[0], B[3]);
  and and_5 (PP0[4], A[0], B[4]);
  and and_6 (PP0[5], A[0], B[5]);
  and and_7 (PP0[6], A[0], B[6]);
  and and_8 (PP0[7], A[0], B[7]);
  somador9bits somador9bits_2 (
    .A({somador9bits_1_o[8], p8_t, p7_t, p6_t, p5_t, p4_t, p3_t, p2_t, p1_t}), .B({1'b0, PP2}),
    .O(somador9bits_2_o[8]), .S({P8, P7, P6, P5, P4, P3, P2, P1, AC[2]}));
  and and_9 (PP1[0], A[1], B[0]);
  and and_10 (PP1[1], A[1], B[1]);
  and and_11 (PP1[2], A[1], B[2]);
  and and_12 (PP1[3], A[1], B[3]);
  and and_13 (PP1[4], A[1], B[4]);
  and and_14 (PP1[5], A[1], B[5]);
  and and_15 (PP1[6], A[1], B[6]);
  and and_16 (PP1[7], A[1], B[7]);
  somador9bits somador9bits_3 (
    .A({somador9bits_2_o[8], P8, P7, P6, P5, P4, P3, P2, P1}), .B({1'b0, PP3}), .O(somador9bits_3_o[8]),
    .S({L8, L7, L6, L5, L4, L3, L2, L1, AC[3]}));
  and and_17 (PP2[0], A[2], B[0]);
  and and_18 (PP2[1], A[2], B[1]);
  and and_19 (PP2[2], A[2], B[2]);
  and and_20 (PP2[3], A[2], B[3]);
  and and_21 (PP2[4], A[2], B[4]);
  and and_22 (PP2[5], A[2], B[5]);
  and and_23 (PP2[6], A[2], B[6]);
  and and_24 (PP2[7], A[2], B[7]);
  somador9bits somador9bits_4 (
    .A({somador9bits_3_o[8], L8, L7, L6, L5, L4, L3, L2, L1}), .B({1'b0, PP4}), .O(somador9bits_4_o[8]),
    .S({l8_t, l7_t, l6_t, l5_t, l4_t, l3_t, l2_t, l1_t, AC[4]}));
  somador9bits somador9bits_5 (
    .A({somador9bits_4_o[8], l8_t, l7_t, l6_t, l5_t, l4_t, l3_t, l2_t, l1_t}), .B({1'b0, PP5}),
    .O(somador9bits_5_o[8]), .S({H8, H7, H6, H5, H4, H3, H2, H1, AC[5]}));
  and and_25 (PP3[0], A[3], B[0]);
  and and_26 (PP3[1], A[3], B[1]);
  and and_27 (PP3[2], A[3], B[2]);
  and and_28 (PP3[3], A[3], B[3]);
  and and_29 (PP3[4], A[3], B[4]);
  and and_30 (PP3[5], A[3], B[5]);
  and and_31 (PP3[6], A[3], B[6]);
  and and_32 (PP3[7], A[3], B[7]);
  somador9bits somador9bits_6 (
    .A({somador9bits_5_o[8], H8, H7, H6, H5, H4, H3, H2, H1}), .B({1'b0, PP6}), .O(somador9bits_6_o[8]),
    .S({h8_t, h7_t, h6_t, h5_t, h4_t, h3_t, h2_t, h1_t, AC[6]}));
  and and_33 (PP4[0], A[4], B[0]);
  and and_34 (PP4[1], A[4], B[1]);
  and and_35 (PP4[2], A[4], B[2]);
  and and_36 (PP4[3], A[4], B[3]);
  and and_37 (PP4[4], A[4], B[4]);
  and and_38 (PP4[5], A[4], B[5]);
  and and_39 (PP4[6], A[4], B[6]);
  and and_40 (PP4[7], A[4], B[7]);
  somador9bits somador9bits_7 (
    .A({somador9bits_6_o[8], h8_t, h7_t, h6_t, h5_t, h4_t, h3_t, h2_t, h1_t}), .B({1'b0, PP7}), .O(W0),
    .S({MQ, AC[7]}));
  and and_41 (PP5[0], A[5], B[0]);
  and and_42 (PP5[1], A[5], B[1]);
  and and_43 (PP5[2], A[5], B[2]);
  and and_44 (PP5[3], A[5], B[3]);
  and and_45 (PP5[4], A[5], B[4]);
  and and_46 (PP5[5], A[5], B[5]);
  and and_47 (PP5[6], A[5], B[6]);
  and and_48 (PP5[7], A[5], B[7]);
  and and_49 (PP6[0], A[6], B[0]);
  and and_50 (PP6[1], A[6], B[1]);
  and and_51 (PP6[2], A[6], B[2]);
  and and_52 (PP6[3], A[6], B[3]);
  and and_53 (PP6[4], A[6], B[4]);
  and and_54 (PP6[5], A[6], B[5]);
  and and_55 (PP6[6], A[6], B[6]);
  and and_56 (PP6[7], A[6], B[7]);
  and and_57 (PP7[0], A[7], B[0]);
  and and_58 (PP7[1], A[7], B[1]);
  and and_59 (PP7[2], A[7], B[2]);
  and and_60 (PP7[3], A[7], B[3]);
  and and_61 (PP7[4], A[7], B[4]);
  and and_62 (PP7[5], A[7], B[5]);
  and and_63 (PP7[6], A[7], B[6]);
  and and_64 (PP7[7], A[7], B[7]);

  // Other names for the same wires on the sheet: p0_t = AC[1]; P0 = AC[2]; L0 = AC[3]; l0_t = AC[4]; H0 = AC[5];
  //   h0_t = AC[6]; Z0 = AC[7]; Z1 = MQ[0]; Z2 = MQ[1]; Z3 = MQ[2]; Z4 = MQ[3]; Z5 = MQ[4]; Z6 = MQ[5]; Z7 = MQ[6];
  //   Z8 = MQ[7]; Q0 = PP4[0]; q0_t = PP5[0]; Q1 = PP4[1]; q1_t = PP5[1]; Q2 = PP4[2]; q2_t = PP5[2]; Q3 = PP4[3];
  //   q3_t = PP5[3]; Q4 = PP4[4]; q4_t = PP5[4]; Q5 = PP4[5]; q5_t = PP5[5]; Q6 = PP4[6]; q6_t = PP5[6]; Q7 = PP4[7];
  //   q7_t = PP5[7]; PP0[0] = AC[0]; R0 = AC[0]; r0_t = PP1[0]; R1 = PP0[1]; r1_t = PP1[1]; R2 = PP0[2];
  //   r2_t = PP1[2]; R3 = PP0[3]; r3_t = PP1[3]; R4 = PP0[4]; r4_t = PP1[4]; R5 = PP0[5]; r5_t = PP1[5]; R6 = PP0[6];
  //   r6_t = PP1[6]; R7 = PP0[7]; r7_t = PP1[7]; S0 = PP2[0]; s0_t = PP3[0]; S1 = PP2[1]; s1_t = PP3[1]; S2 = PP2[2];
  //   s2_t = PP3[2]; S3 = PP2[3]; s3_t = PP3[3]; S4 = PP2[4]; s4_t = PP3[4]; S5 = PP2[5]; s5_t = PP3[5]; S6 = PP2[6];
  //   s6_t = PP3[6]; S7 = PP2[7]; s7_t = PP3[7]; T0 = PP6[0]; t0_t = PP7[0]; T1 = PP6[1]; t1_t = PP7[1]; T2 = PP6[2];
  //   t2_t = PP7[2]; T3 = PP6[3]; t3_t = PP7[3]; T4 = PP6[4]; t4_t = PP7[4]; T5 = PP6[5]; t5_t = PP7[5]; T6 = PP6[6];
  //   t6_t = PP7[6]; T7 = PP6[7]; t7_t = PP7[7]
endmodule
