// Digital circuit somador8bits.dig as structural Verilog
module somador8bits (
  input  [7:0] A,
  input  [7:0] B,
  input  Cin,
  output [7:0] S,
  output Cout
);

  wire somador1bit_1_cout, somador1bit_2_cout, somador1bit_3_cout, somador1bit_4_cout, somador1bit_5_cout,
       somador1bit_6_cout, somador1bit_7_cout;

  somador1bit somador1bit_1 (.A(A[0]), .B(B[0]), .Cin(Cin), .S(S[0]), .Cout(somador1bit_1_cout));
  somador1bit somador1bit_2 (.A(A[1]), .B(B[1]), .Cin(somador1bit_1_cout), .S(S[1]), .Cout(somador1bit_2_cout));
  somador1bit somador1bit_3 (.A(A[2]), .B(B[2]), .Cin(somador1bit_2_cout), .S(S[2]), .Cout(somador1bit_3_cout));
  somador1bit somador1bit_4 (.A(A[3]), .B(B[3]), .Cin(somador1bit_3_cout), .S(S[3]), .Cout(somador1bit_4_cout));
  somador1bit somador1bit_5 (.A(A[4]), .B(B[4]), .Cin(somador1bit_4_cout), .S(S[4]), .Cout(somador1bit_5_cout));
  somador1bit somador1bit_6 (.A(A[5]), .B(B[5]), .Cin(somador1bit_5_cout), .S(S[5]), .Cout(somador1bit_6_cout));
  somador1bit somador1bit_7 (.A(A[6]), .B(B[6]), .Cin(somador1bit_6_cout), .S(S[6]), .Cout(somador1bit_7_cout));
  somador1bit somador1bit_8 (.A(A[7]), .B(B[7]), .Cin(somador1bit_7_cout), .S(S[7]), .Cout(Cout));
endmodule
