// Digital circuit somador9bits.dig as structural Verilog
module somador9bits (
  input  [8:0] A,
  input  [8:0] B,
  output O,
  output [8:0] S
);

  wire somador1bit_2_cout, somador1bit_3_cout, somador1bit_4_cout, somador1bit_5_cout, somador1bit_6_cout,
       somador1bit_7_cout, somador1bit_8_cout, somador1bit_9_cout;

  somador1bit somador1bit_1 (.A(A[8]), .B(B[8]), .Cin(somador1bit_2_cout), .S(S[8]), .Cout(O));
  somador1bit somador1bit_2 (.A(A[7]), .B(B[7]), .Cin(somador1bit_3_cout), .S(S[7]), .Cout(somador1bit_2_cout));
  somador1bit somador1bit_3 (.A(A[6]), .B(A[6]), .Cin(somador1bit_4_cout), .S(S[6]), .Cout(somador1bit_3_cout));
  somador1bit somador1bit_4 (.A(A[5]), .B(B[5]), .Cin(somador1bit_5_cout), .S(S[5]), .Cout(somador1bit_4_cout));
  somador1bit somador1bit_5 (.A(A[4]), .B(B[4]), .Cin(somador1bit_6_cout), .S(S[4]), .Cout(somador1bit_5_cout));
  somador1bit somador1bit_6 (.A(A[3]), .B(B[3]), .Cin(somador1bit_7_cout), .S(S[3]), .Cout(somador1bit_6_cout));
  somador1bit somador1bit_7 (.A(A[2]), .B(B[2]), .Cin(somador1bit_8_cout), .S(S[2]), .Cout(somador1bit_7_cout));
  somador1bit somador1bit_8 (.A(A[1]), .B(B[1]), .Cin(somador1bit_9_cout), .S(S[1]), .Cout(somador1bit_8_cout));
  somador1bit somador1bit_9 (.A(A[0]), .B(B[0]), .Cin(1'b0), .S(S[0]), .Cout(somador1bit_9_cout));

  assign B[6] = A[6];

  // Other names for the same wires on the sheet: B6 = A[6]
endmodule
